// Logisim project 2 way traffic light system.circ as structural Verilog: 1 circuit, main circuit main
module main (
);

  wire A_q, A_qn, and_1_out, and_2_out, and_3_out, and_4_out, and_5_out, and_6_out, and_7_out, and_8_out,
       and_9_out, and_10_out, and_11_out, and_12_out, and_13_out, and_14_out, B_q, B_qn, C_q, C_qn,
       clock_1_out, not_1_out, not_2_out, or_1_out, or_2_out, or_3_out, or_4_out, or_5_out;

  Clock clock_1 (.out(clock_1_out));
  or or_1 (or_1_out, and_1_out, and_2_out);
  and and_1 (and_1_out, C_q, B_qn, A_qn);
  and and_2 (and_2_out, C_qn, B_q, A_q);
  D_Flip_Flop C (.clk(clock_1_out), .D(or_1_out), .Q(C_q), .Qn(C_qn));  // open: preset, en, reset
  or or_2 (or_2_out, and_3_out, and_4_out);
  and and_3 (and_3_out, C_qn, B_qn, A_q);
  D_Flip_Flop B (.clk(clock_1_out), .D(or_2_out), .Q(B_q), .Qn(B_qn));  // open: preset, en, reset
  and and_4 (and_4_out, C_qn, B_q, A_qn);
  or or_3 (or_3_out, and_6_out, and_7_out);
  and and_5 (and_5_out, C_q, B_qn, A_qn);
  and and_6 (and_6_out, B_qn, A_qn);
  D_Flip_Flop A (.clk(clock_1_out), .D(or_3_out), .Q(A_q), .Qn(A_qn));  // open: preset, en, reset
  and and_7 (and_7_out, C_qn, A_qn);
  and and_8 (and_8_out, C_q, B_qn, A_q);
  or or_4 (or_4_out, and_8_out, and_5_out);
  and and_9 (and_9_out, C_q, B_qn, A_q);
  and and_10 (and_10_out, C_q, B_qn, A_qn);
  and and_11 (and_11_out, C_qn, B_qn, A_q);
  and and_12 (and_12_out, C_qn, B_q, A_qn);
  or or_5 (or_5_out, and_11_out, and_12_out);
  and and_13 (and_13_out, C_qn, B_q, A_qn);
  and and_14 (and_14_out, C_qn, B_qn, A_q);
  LED R1 (.in(not_1_out));
  not not_1 (not_1_out, or_4_out);
  LED Y1 (.in(and_9_out));
  LED G1 (.in(and_10_out));
  LED R2 (.in(not_2_out));
  not not_2 (not_2_out, or_5_out);
  LED Y2 (.in(and_13_out));
  LED G2 (.in(and_14_out));
endmodule
